// Logisim project 21.circ as structural Verilog: 2 circuits, main circuit main
module main (
);

  wire and_1_out, and_2_out, and_3_out, and_4_out, and_5_out, and_6_out, and_11_out, and_15_out, and_16_out,
       and_17_out, and_18_out, C0, C1, C2, CLR_SC, D0, D1, D2, D3, D4, D5, D6, DR_Zero, INC_DR, INC_PC,
       LD_AC, LD_AR, LD_DR, LD_PC, MEM_READ, MEM_WRITE, or_1_out, or_7_out, or_8_out, or_9_out, or_10_out,
       or_11_out, or_12_out, or_14_out, or_15_out, Q, S0, S1, S2, Select_ALU, T, T0, T1, T2, T3, T4, T5, T6,
       T7;
  wire [2:0] SC_q;
  wire [7:0] _11_4, AR_q, bit_extender_2_out, Bits, Bus, PC_q;
  wire [15:0] AC, alu_1_output, bit_extender_3_out, bit_extender_4_out, DR, IR, multiplexer_4_out, MUX_AC,
       MUX_DR, ram_1_data, TR_q;

  Decoder #(.select(4), .enable("false")) decoder_1 (
    .out0(D0), .out1(D1), .out2(D2), .out3(D3), .out4(D4), .out5(D5), .out6(D6), .sel(IR[15:12]));  // open: out7, out8, out9, out10, out11, out12, out13, out14, out15
  Counter #(.width(3), .max('h7)) SC (.load(1'b0), .count(1'b1), .Q(SC_q), .clk(T), .clr(Q));  // open: D, carry
  Decoder #(.select(3), .enable("false")) decoder_2 (
    .out0(T0), .out1(T1), .out2(T2), .out3(T3), .out4(T4), .out5(T5), .out6(T6), .out7(T7), .sel(SC_q));
  or or_1 (or_1_out, D0, D1, D2, D5, D6);
  and and_1 (and_1_out, D3, T3);
  and and_2 (and_2_out, D6, T5);
  and and_3 (and_3_out, D3, T3);
  and and_4 (and_4_out, D6, T5);
  and and_5 (and_5_out, D4, T3);
  nor nor_1 (DR_Zero, DR[15], DR[14], DR[13], DR[12], DR[11], DR[10], DR[9], DR[8], DR[7], DR[6], DR[5], DR[4], DR[3], DR[2], DR[1], DR[0]);
  D_Flip_Flop d_ff_1 (.clk(T), .D(CLR_SC), .Q(Q));  // open: Qn, preset, en, reset
  and and_6 (and_6_out, T3, or_1_out);
  or or_2 (MEM_WRITE, and_1_out, and_2_out);
  or or_3 (S2, and_3_out, and_4_out, T2);
  or or_4 (S1, and_5_out, T2, T0);
  or or_5 (MEM_READ, and_6_out, T1);
  or or_6 (LD_AR, T0, T2);
  or or_7 (or_7_out, D0, D1, D2, D5, D6);
  and and_7 (INC_DR, D6, T4);
  or or_8 (or_8_out, D0, D1, D2, D5);
  and and_8 (LD_PC, D4, T3);
  and and_9 (LD_DR, or_7_out, T3);
  and and_10 (LD_AC, or_8_out, T4);
  or or_9 (or_9_out, D0, D1, D2, D3, D5, D6);
  or or_10 (or_10_out, D0, D5);
  or or_11 (or_11_out, D0, D1);
  and and_11 (and_11_out, or_9_out, T3);
  or or_12 (or_12_out, D0, D2, D5);
  or or_13 (S0, and_11_out, T1, T0);
  and and_12 (C2, or_10_out, T4);
  and and_13 (C1, or_11_out, T4);
  and and_14 (C0, or_12_out, T4);
  and and_15 (and_15_out, D6, T5, DR_Zero);
  or or_14 (or_14_out, D0, D1, D2, D5);
  or or_15 (or_15_out, D3, D4);
  and ALU_swap (Select_ALU, D5, T4);
  or or_16 (INC_PC, and_15_out, T1);
  and and_16 (and_16_out, or_14_out, T4);
  and and_17 (and_17_out, or_15_out, T3);
  and and_18 (and_18_out, D6, T5);
  Multiplexer #(.width(16), .enable("false")) multiplexer_1 (.in0(DR), .in1(AC), .out(MUX_DR), .sel(Select_ALU));
  Multiplexer #(.width(16), .enable("false")) multiplexer_2 (.in0(AC), .in1(DR), .out(MUX_AC), .sel(Select_ALU));
  or or_17 (CLR_SC, and_16_out, and_17_out, and_18_out);
  Multiplexer #(.width(8), .enable("false")) multiplexer_3 (.in0(Bus), .in1(_11_4), .out(Bits), .sel(T2));
  Clock clock_1 (.out(T));
  Bit_Extender #(.in_width(16), .out_width(8)) bit_extender_1 (.in(multiplexer_4_out), .out(Bus));
  // Probe on Bits
  Bit_Extender #(.in_width(16), .out_width(8)) bit_extender_2 (.in(multiplexer_4_out), .out(bit_extender_2_out));
  ALU alu_1 (.DR(MUX_DR), .AC(MUX_AC), .C2C1C0({C2, C1, C0}), .Output(alu_1_output));
  Counter AR (.load(LD_AR), .D(Bits), .count(1'b0), .Q(AR_q), .clk(T), .clr(1'b0));  // open: carry
  Counter PC (.load(LD_PC), .D(bit_extender_2_out), .count(INC_PC), .Q(PC_q), .clk(T), .clr(1'b0));  // open: carry
  Counter #(.width(16), .max('hffff)) u_DR (
    .load(LD_DR), .D(multiplexer_4_out), .count(INC_DR), .Q(DR), .clk(T), .clr(1'b0));  // open: carry
  Counter #(.width(16), .max('hffff)) u_AC (
    .load(LD_AC), .D(alu_1_output), .count(1'b0), .Q(AC), .clk(T), .clr(1'b0));  // open: carry
  Counter #(.width(16), .max('hffff)) u_IR (
    .load(T1), .D(multiplexer_4_out), .count(1'b0), .Q({IR[15:12], _11_4, IR[3:0]}), .clk(T), .clr(1'b0));  // open: carry
  Counter #(.width(16), .max('hffff)) TR (
    .load(1'b0), .D(multiplexer_4_out), .count(1'b0), .Q(TR_q), .clk(T), .clr(1'b0));  // open: carry
  RAM #(.dataWidth(16), .bus("separate")) ram_1 (
    .addr(AR_q), .din(multiplexer_4_out), .data(ram_1_data), .str(MEM_WRITE), .clk(T), .ld(MEM_READ));  // open: sel, clr
  assign bit_extender_3_out = {{8{1'b0}}, AR_q};  // Bit_Extender bit_extender_3
  assign bit_extender_4_out = {{8{1'b0}}, PC_q};  // Bit_Extender bit_extender_4
  Multiplexer #(.select(3), .width(16), .enable("false")) multiplexer_4 (
    .in1(ram_1_data), .in2(bit_extender_3_out), .in3(bit_extender_4_out), .in4(DR), .in5(AC),
    .in6({IR[15:12], _11_4, IR[3:0]}), .in7(TR_q), .out(multiplexer_4_out), .sel({S2, S1, S0}));  // open: in0

  // Other names for the same wires on the sheet: IR[11:4] = _11_4
endmodule

module ALU (
  input  [15:0] DR,
  input  [15:0] AC,
  input  [2:0] C2C1C0,
  output [15:0] Output
);

  wire [15:0] adder_1_out, divider_1_out, multiplier_1_out, not_1_out, subtractor_1_out, xor_1_out;

  Divider #(.width(16)) divider_1 (.a(DR), .b(AC), .out(divider_1_out));  // open: upper, rem
  Adder #(.width(16)) adder_1 (.a(DR), .b(AC), .out(adder_1_out));  // open: cin, cout
  Subtractor #(.width(16)) subtractor_1 (.a(DR), .b(AC), .out(subtractor_1_out));  // open: bin, bout
  Multiplier #(.width(16)) multiplier_1 (.a(DR), .b(AC), .out(multiplier_1_out));  // open: cin, cout
  assign not_1_out = ~DR;  // NOT_Gate not_1, 16 bits wide
  assign xor_1_out = DR ^ AC;  // XOR_Gate xor_1, 16 bits wide
  Multiplexer #(.select(3), .width(16), .enable("false")) multiplexer_1 (
    .in1(DR), .in2(adder_1_out), .in3(subtractor_1_out), .in4(multiplier_1_out), .in5(divider_1_out),
    .in6(not_1_out), .in7(xor_1_out), .out(Output), .sel(C2C1C0));  // open: in0
endmodule
